// Logisim project part2.circ as structural Verilog: 1 circuit, main circuit my circuit
module my_circuit (
  input  [3:0] in_1,
  input  [1:0] in_2,
  input  [3:0] in_3,
  output [7:0] out_4,
  output [1:0] out_5
);

  wire button_1_out, clock_1_out;

  Register register_1 (.D({in_1, in_3}), .Q(out_4), .clk(clock_1_out), .clr(button_1_out));  // open: en
  Button button_1 (.out(button_1_out));
  Clock clock_1 (.out(clock_1_out));
  Multiplexer #(.select(2), .width(2), .disabled(0), .enable("false")) multiplexer_1 (
    .in0(out_4[1:0]), .in1(out_4[3:2]), .in2(out_4[5:4]), .in3(out_4[7:6]), .out(out_5), .sel(in_2));

  // Notes on the sheet:
  //   Dan Sun
  //   8/24/2014
endmodule
