// Logisim project hw3.circ as structural Verilog: 5 circuits, main circuit 16-bit ALU
module _1_bit_full_adder (
  input  CarryIn,
  input  A,
  input  B,
  output Sum,
  output CarryOut
);

  wire and_1_out, and_2_out, and_3_out, and_4_out, and_5_out, and_6_out, and_7_out, not_1_out, not_2_out,
       not_3_out;

  and and_1 (and_1_out, CarryIn, not_2_out, not_3_out);
  not not_1 (not_1_out, CarryIn);
  and and_2 (and_2_out, not_1_out, A, not_3_out);
  or or_1 (Sum, and_1_out, and_2_out, and_3_out, and_4_out);
  not not_2 (not_2_out, A);
  and and_3 (and_3_out, not_1_out, not_2_out, B);
  and and_4 (and_4_out, CarryIn, A, B);
  and and_5 (and_5_out, CarryIn, A);
  not not_3 (not_3_out, B);
  or or_2 (CarryOut, and_4_out, and_5_out, and_6_out, and_7_out);
  and and_6 (and_6_out, CarryIn, B);
  and and_7 (and_7_out, A, B);

  // Notes on the sheet:
  //   Dan Sun\n9 / 7 / 2014
endmodule

module _4_bit_full_adder (
  input  [3:0] A,
  input  [3:0] B,
  input  CarryIn,
  output [3:0] Sum,
  output CarryOut
);

  wire n1_bit_full_adder_2_carryout, n1_bit_full_adder_3_carryout, n1_bit_full_adder_4_carryout;

  _1_bit_full_adder u_1_bit_full_adder_1 (
    .CarryIn(n1_bit_full_adder_2_carryout), .A(A[3]), .B(B[3]), .Sum(Sum[3]), .CarryOut(CarryOut));
  _1_bit_full_adder u_1_bit_full_adder_2 (
    .CarryIn(n1_bit_full_adder_3_carryout), .A(A[2]), .B(B[2]), .Sum(Sum[2]),
    .CarryOut(n1_bit_full_adder_2_carryout));
  _1_bit_full_adder u_1_bit_full_adder_3 (
    .CarryIn(n1_bit_full_adder_4_carryout), .A(A[1]), .B(B[1]), .Sum(Sum[1]),
    .CarryOut(n1_bit_full_adder_3_carryout));
  _1_bit_full_adder u_1_bit_full_adder_4 (
    .CarryIn(CarryIn), .A(A[0]), .B(B[0]), .Sum(Sum[0]), .CarryOut(n1_bit_full_adder_4_carryout));

  // Notes on the sheet:
  //   Dan Sun\n9 / 7 / 2014
endmodule

module _16_bit_full_adder (
  input  [15:0] A,
  input  [15:0] B,
  input  CarryIn,
  output [15:0] Sum,
  output CarryOut
);

  wire n4_bit_full_adder_2_carryout, n4_bit_full_adder_3_carryout, n4_bit_full_adder_4_carryout;

  _4_bit_full_adder u_4_bit_full_adder_1 (
    .A(A[15:12]), .B(B[15:12]), .CarryIn(n4_bit_full_adder_2_carryout), .Sum(Sum[15:12]), .CarryOut(CarryOut));
  _4_bit_full_adder u_4_bit_full_adder_2 (
    .A(A[11:8]), .B(B[11:8]), .CarryIn(n4_bit_full_adder_3_carryout), .Sum(Sum[11:8]),
    .CarryOut(n4_bit_full_adder_2_carryout));
  _4_bit_full_adder u_4_bit_full_adder_3 (
    .A(A[7:4]), .B(B[7:4]), .CarryIn(n4_bit_full_adder_4_carryout), .Sum(Sum[7:4]),
    .CarryOut(n4_bit_full_adder_3_carryout));
  _4_bit_full_adder u_4_bit_full_adder_4 (
    .A(A[3:0]), .B(B[3:0]), .CarryIn(CarryIn), .Sum(Sum[3:0]), .CarryOut(n4_bit_full_adder_4_carryout));

  // Notes on the sheet:
  //   Dan Sun\n9 / 7 / 2014
endmodule

module _4_bit_ALU (
  input  [3:0] A,
  input  [3:0] B,
  input  S2,
  input  S1,
  input  S0,
  output out_6,
  output out_7,
  output out_8,
  output [3:0] Output,
  output out_10,
  output out_11
);

  wire [3:0] A___1, A___B, A___B_t, A___B_t_t, A___B_t_t_t, A___B_t_t_t_t, minus_A, not_1_out, not_2_out;

  assign not_1_out = ~A;  // NOT_Gate not_1, 4 bits wide
  assign not_2_out = ~B;  // NOT_Gate not_2, 4 bits wide
  _4_bit_full_adder u_4_bit_full_adder_1 (.A(A), .B(B), .CarryIn(1'b0), .Sum(A___B_t), .CarryOut(out_6));
  _4_bit_full_adder u_4_bit_full_adder_2 (.A(not_1_out), .B(4'b0001), .CarryIn(1'b0), .Sum(minus_A), .CarryOut(out_10));
  assign A___B = A & B;  // AND_Gate and_1, 4 bits wide
  _4_bit_full_adder u_4_bit_full_adder_3 (.A(A), .B(not_2_out), .CarryIn(1'b1), .Sum(A___B_t_t), .CarryOut(out_7));
  assign A___B_t_t_t_t = A | B;  // OR_Gate or_1, 4 bits wide
  _4_bit_full_adder u_4_bit_full_adder_4 (.A(A), .B(4'b0001), .CarryIn(1'b0), .Sum(A___1), .CarryOut(out_8));
  assign A___B_t_t_t = A ^ B;  // XOR_Gate xor_1, 4 bits wide
  Multiplexer #(.select(3), .width(4), .disabled(0), .enable("false")) multiplexer_1 (
    .in0(A___B_t), .in1(A___B_t_t), .in2(A___1), .in3(minus_A), .in4({1'b0, A[3:1]}), .in5(A___B),
    .in6(A___B_t_t_t_t), .in7(A___B_t_t_t), .out(Output), .sel({S2, S1, S0}));

  assign out_11 = A[0];

  // Other names for the same wires on the sheet: A____1[2:0] = A[3:1]

  // Notes on the sheet:
  //   Dan Sun
  //   9/7/2014
endmodule

module _16_bit_ALU (
  input  [15:0] A,
  input  [15:0] B,
  input  S2,
  input  S1,
  input  S0,
  output out_6,
  output out_7,
  output out_8,
  output [15:0] Output,
  output out_10,
  output out_11
);

  wire [15:0] A___1, A___B, A___B_t, A___B_t_t, A___B_t_t_t, A___B_t_t_t_t, minus_A, not_1_out, not_2_out;

  assign not_1_out = ~A;  // NOT_Gate not_1, 16 bits wide
  assign not_2_out = ~B;  // NOT_Gate not_2, 16 bits wide
  _16_bit_full_adder u_16_bit_full_adder_1 (.A(A), .B(B), .CarryIn(1'b0), .Sum(A___B_t), .CarryOut(out_6));
  _16_bit_full_adder u_16_bit_full_adder_2 (.A(not_1_out), .B(16'h1), .CarryIn(1'b0), .Sum(minus_A), .CarryOut(out_10));
  assign A___B = A & B;  // AND_Gate and_1, 16 bits wide
  _16_bit_full_adder u_16_bit_full_adder_3 (.A(A), .B(not_2_out), .CarryIn(1'b1), .Sum(A___B_t_t), .CarryOut(out_7));
  assign A___B_t_t_t_t = A | B;  // OR_Gate or_1, 16 bits wide
  _16_bit_full_adder u_16_bit_full_adder_4 (.A(A), .B(16'h1), .CarryIn(1'b0), .Sum(A___1), .CarryOut(out_8));
  assign A___B_t_t_t = A ^ B;  // XOR_Gate xor_1, 16 bits wide
  Multiplexer #(.select(3), .width(16), .disabled(0), .enable("false")) multiplexer_1 (
    .in0(A___B_t), .in1(A___B_t_t), .in2(A___1), .in3(minus_A), .in4({1'b0, A[15:1]}), .in5(A___B),
    .in6(A___B_t_t_t_t), .in7(A___B_t_t_t), .out(Output), .sel({S2, S1, S0}));

  assign out_11 = A[0];

  // Other names for the same wires on the sheet: A____1[14:0] = A[15:1]

  // Notes on the sheet:
  //   Dan Sun
  //   9 / 7 / 2014
endmodule
