// Logisim project hw4part2.circ as structural Verilog: 2 circuits, main circuit One-Hot State Machine
module Tester (
  input  G
);

  wire Clock_out, one_hot_state_machine_1_w, one_hot_state_machine_1_x, one_hot_state_machine_1_y,
       one_hot_state_machine_1_z, Reset_out;

  One_Hot_State_Machine one_hot_state_machine_1 (
    .W(one_hot_state_machine_1_w), .Clock(Clock_out), .Reset(Reset_out), .G(G),
    .X(one_hot_state_machine_1_x), .Y(one_hot_state_machine_1_y), .Z(one_hot_state_machine_1_z));
  Clock Clock (.out(Clock_out));
  LED W (.in(one_hot_state_machine_1_w));
  LED X (.in(one_hot_state_machine_1_x));
  LED Y (.in(one_hot_state_machine_1_y));
  LED Z (.in(one_hot_state_machine_1_z));
  Button Reset (.out(Reset_out));

  // Notes on the sheet:
  //   You can use this to test your circuit.
endmodule

module One_Hot_State_Machine (
  input  G,
  input  Clock,
  input  Reset,
  output W,
  output X,
  output Y,
  output Z
);

  wire and_1_out, and_2_out, and_3_out, and_4_out, and_5_out, and_6_out, and_7_out, and_8_out, and_9_out,
       and_10_out, nor_1_out, not_1_out, or_1_out, or_3_out, or_7_out, or_8_out, S0_q, S1_q, S2_q, S3_q,
       S4_q, S5_q, S6_q;

  or or_1 (or_1_out, and_1_out, nor_1_out, and_8_out);
  Register #(.width(1)) S0 (.D(or_1_out), .en(1'b1), .Q(S0_q), .clk(Clock), .clr(Reset));
  not not_1 (not_1_out, G);
  or or_2 (X, S0_q, S3_q);
  Register #(.width(1)) S1 (.D(and_4_out), .en(1'b1), .Q(S1_q), .clk(Clock), .clr(Reset));
  or or_3 (or_3_out, S2_q, and_10_out, and_5_out);
  Register #(.width(1)) S2 (.D(and_3_out), .en(1'b1), .Q(S2_q), .clk(Clock), .clr(Reset));
  or or_4 (Z, S2_q, S4_q, S5_q);
  or or_5 (W, S2_q, S3_q, S6_q);
  Register #(.width(1)) S3 (.D(or_3_out), .en(1'b1), .Q(S3_q), .clk(Clock), .clr(Reset));
  Register #(.width(1)) S4 (.D(and_7_out), .en(1'b1), .Q(S4_q), .clk(Clock), .clr(Reset));
  or or_6 (Y, S3_q, S5_q, S6_q);
  or or_7 (or_7_out, and_6_out, and_2_out);
  Register #(.width(1)) S5 (.D(or_7_out), .en(1'b1), .Q(S5_q), .clk(Clock), .clr(Reset));
  or or_8 (or_8_out, S5_q, and_9_out);
  and and_1 (and_1_out, S0_q, not_1_out);
  Register #(.width(1)) S6 (.D(or_8_out), .en(1'b1), .Q(S6_q), .clk(Clock), .clr(Reset));
  and and_2 (and_2_out, G, S3_q);
  and and_3 (and_3_out, S1_q, not_1_out);
  and and_4 (and_4_out, S0_q, G);
  and and_5 (and_5_out, not_1_out, S3_q);
  and and_6 (and_6_out, S4_q, G);
  and and_7 (and_7_out, S1_q, G);
  and and_8 (and_8_out, not_1_out, S6_q);
  and and_9 (and_9_out, G, S6_q);
  nor nor_1 (nor_1_out, S6_q, S5_q, S4_q, S3_q, S2_q, S1_q, S0_q);
  and and_10 (and_10_out, S4_q, not_1_out);

  // Other names for the same wires on the sheet: CLK = Clock; RST = Reset

  // Notes on the sheet:
  //   My name is
  //   Dan Sun
  //   and this is my pretty one-hot state machine!
  //   Implement your one-hot state machine circuit here!
endmodule
