// Logisim project hw4part3.circ as structural Verilog: 2 circuits, main circuit Reduced State Machine
module Tester (
  input  G
);

  wire Clock_out, reduced_state_machine_1_w, reduced_state_machine_1_x, reduced_state_machine_1_y,
       reduced_state_machine_1_z, Reset_out;

  Reduced_State_Machine reduced_state_machine_1 (
    .W(reduced_state_machine_1_w), .Clock(Clock_out), .Reset(Reset_out), .G(G),
    .X(reduced_state_machine_1_x), .Y(reduced_state_machine_1_y), .Z(reduced_state_machine_1_z));
  Clock Clock (.out(Clock_out));
  LED W (.in(reduced_state_machine_1_w));
  LED X (.in(reduced_state_machine_1_x));
  LED Y (.in(reduced_state_machine_1_y));
  LED Z (.in(reduced_state_machine_1_z));
  Button Reset (.out(Reset_out));

  // Notes on the sheet:
  //   You can use this to test your circuit.
endmodule

module Reduced_State_Machine (
  input  G,
  input  Clock,
  input  Reset,
  output W,
  output X,
  output Y,
  output Z
);

  wire and_1_out, and_2_out, and_3_out, and_4_out, and_5_out, and_6_out, and_7_out, and_8_out, and_9_out,
       and_10_out, and_11_out, and_12_out, and_13_out, and_14_out, and_15_out, and_16_out, N0_out, N1_out,
       N2_out, not_1_out, not_2_out, not_3_out, not_4_out, S0_q, S2_q;

  and and_1 (and_1_out, G, S2_q);
  and and_2 (and_2_out, S2_q, S0_q);
  or N2 (N2_out, and_1_out, and_2_out, and_4_out);
  not not_1 (not_1_out, G);
  and and_3 (and_3_out, not_1_out, S0_q);
  and and_4 (and_4_out, G, S0_q);
  Register #(.width(1)) S2 (.D(N2_out), .en(1'b1), .Q(S2_q), .clk(Clock), .clr(Reset));
  and and_5 (and_5_out, not_1_out, S2_q, not_3_out);
  and and_6 (and_6_out, not_2_out, W, not_4_out);
  or N1 (N1_out, and_3_out, and_2_out, and_5_out, and_6_out, and_8_out);
  not not_2 (not_2_out, S2_q);
  and and_7 (and_7_out, S2_q, not_3_out, not_4_out);
  and and_8 (and_8_out, G, W, not_4_out);
  and and_9 (and_9_out, not_2_out, W);
  and and_10 (and_10_out, G, not_3_out, not_4_out);
  or N0 (N0_out, and_7_out, and_10_out, and_9_out);
  Register #(.width(1)) S1 (.D(N1_out), .en(1'b1), .Q(W), .clk(Clock), .clr(Reset));
  not not_3 (not_3_out, W);
  and and_11 (and_11_out, not_2_out, not_3_out, not_4_out);
  or or_1 (X, and_11_out, and_13_out);
  and and_12 (and_12_out, S2_q, S0_q);
  and and_13 (and_13_out, W, S0_q);
  Register #(.width(1)) S0 (.D(N0_out), .en(1'b1), .Q(S0_q), .clk(Clock), .clr(Reset));
  and and_14 (and_14_out, S2_q, not_3_out);
  and and_15 (and_15_out, S2_q, W);
  or or_2 (Y, and_12_out, and_15_out, and_13_out);
  not not_4 (not_4_out, S0_q);
  and and_16 (and_16_out, not_2_out, W, not_4_out);
  or or_3 (Z, and_14_out, and_16_out);

  // Other names for the same wires on the sheet: CLK = Clock; RST = Reset

  // Notes on the sheet:
  //   My name is
  //   Dan Sun
  //   and this is my pretty reduced state machine!
  //   Implement your reduced state machine circuit here!
endmodule
